# Fritzing sketch fritzing_devresemasi (saved by Fritzing 0.9.3b)
breadboards: 1

parts:
  Parça1 = Arduino Uno (Rev3)
  J1 = Basic Servo
  J2 = Basic Servo
  J3 = Basic Servo
  J4 = Basic Servo
  BAT1 = BC9VPC [package=bc9vpc]  # not connected
  Parça2 = Bluetooth HC-05 Macho

nets:
  N1: Parça1.D9_PWM, J2.pulse
  N2: Parça1.D10_PWM/SS, Parça2.TXD
  N3: Parça1.D3_PWM, J1.pulse
  N4: Parça1.D5_PWM, J4.pulse
  N5: Parça1.D6_PWM, J3.pulse
  5V: Parça1.5V, Parça2.VCC
  GND: Parça1.GND, Parça2.GND
  GND_2: J1.gnd, J2.gnd, J3.gnd, J4.gnd
  VCC: J1.vcc, J2.vcc, J3.vcc, J4.vcc

notes:
  DC 6V
  Barrel Jack
  HC06 bluetooth karti
  kullanildi
